# Fritzing sketch Doan (saved by Fritzing 0.9.2b)
breadboards: 1

parts:
  GY1 = MPU-6050 Board GY-521 [form="♀ (female)" package=THT]
  Part1 = Arduino Nano (Rev3.0)
  Part2 = Bluetooth HC-05 Macho
  S1 = Pushbutton [package="[SMD]"]
  S2 = Pushbutton [package="[SMD]"]
  S3 = Pushbutton [package="[SMD]"]
  S4 = Pushbutton [package="[SMD]"]
  J1 = Piezo Speaker
  U1 = LIPO-1000mAh [package=lipo-1000]
  M1 = DC Motor

nets:
  5V: GY1.pin1, Part1.5V, Part2.VCC
  GND: GY1.pin2, Part1.GND, Part2.GND, J1.pin1, U1.-, M1.pin_1
  N1: GY1.pin3, Part1.A5
  N2: GY1.pin4, Part1.A4
  N3: Part1.D0/RX, Part1.D9, Part1.D10, Part1.D11/MOSI, Part1.D12/MISO, S1.Pin_1, S1.Pin_2, S1.Pin_3, S1.Pin_4, S2.Pin_1, S2.Pin_2, S2.Pin_3, S2.Pin_4, S3.Pin_1, S3.Pin_2, S3.Pin_3, S3.Pin_4, S4.Pin_1, S4.Pin_2, S4.Pin_3, S4.Pin_4
  N4: Part1.D2, Part2.RXD
  N5: Part1.D3, Part2.TXD
  N6: Part1.VIN, U1.+
  N7: Part1.A2, J1.pin2
  N8: Part1.D13/SCK, M1.pin_2

custom parts:
  MPU-6050 Board GY-521: Acelerometro y Giroscopio MPU-6050 Board GY-521
